# Fritzing sketch diagram (saved by Fritzing 0.9.3b)

parts:
  Raspberry_Pi_1 = Raspberry Pi 3 [part_number=RPI-3-V1.2]
  U1 = Module 4 Relais 5V [package="Module 4 Relais 5V"]
  U2 = Module 4 Relais 5V [package="Module 4 Relais 5V"]
  S1 = Round Pushbutton

nets:
  N1: Raspberry_Pi_1.3v3, S1.leg0
  N2: Raspberry_Pi_1.GPIO3, U2.IN1
  N3: Raspberry_Pi_1.GIPO4, U2.IN2
  GND: Raspberry_Pi_1.GND, U1.GND, U2.GND
  N4: Raspberry_Pi_1.GIPO17, U2.IN3
  N5: Raspberry_Pi_1.GIPO27, U2.IN4
  N6: Raspberry_Pi_1.GIPO22, U1.IN1
  N7: Raspberry_Pi_1.GIPO10, U1.IN2
  N8: Raspberry_Pi_1.GIPO9, U1.IN3
  N9: Raspberry_Pi_1.GIPO11, U1.IN4
  N10: Raspberry_Pi_1.GIPO21, S1.leg1
  VCC: Raspberry_Pi_1.5V, U1.VCC, U2.VCC

custom parts:
  Module 4 Relais 5V: Module 4 Relais 5V 4x SPD-06VDC-SD-C
